# Fritzing sketch Rotary Encoders Part (saved by Fritzing 0.9.3b)
breadboards: 1

parts:
  Pro_Micro1 = Pro Micro
  RE1 = Rotary Encoder [package=THT]
  RE2 = Rotary Encoder [package=THT]
  RE3 = Rotary Encoder [package=THT]
  RE4 = Rotary Encoder [package=THT]
  RE5 = Rotary Encoder [package=THT]
  RE6 = Rotary Encoder [package=THT]
  RE7 = Rotary Encoder [package=THT]
  RE8 = Rotary Encoder [package=THT]
  Composant1 = sx1509 breakout  # not connected
  U1 = PCF8575C [package=so-24dw]  # not connected

nets:
  N1: Pro_Micro1.TX1, RE7.EncoderPinB
  N2: Pro_Micro1.RX0, RE7.EncoderPinA
  N3: Pro_Micro1.GND, RE1.EncoderPinC, RE2.EncoderPinC, RE3.EncoderPinC, RE4.EncoderPinC, RE5.EncoderPinC, RE6.EncoderPinC, RE7.EncoderPinC, RE8.EncoderPinC
  N4: Pro_Micro1.D4, RE6.EncoderPinB
  N5: Pro_Micro1.D5, RE6.EncoderPinA
  N6: Pro_Micro1.D6, RE5.EncoderPinB
  N7: Pro_Micro1.D7, RE5.EncoderPinA
  N8: Pro_Micro1.D8, RE4.EncoderPinB
  N9: Pro_Micro1.D9, RE4.EncoderPinA
  N10: Pro_Micro1.D10, RE3.EncoderPinB
  N11: Pro_Micro1.D16/MOSI, RE3.EncoderPinA
  N12: Pro_Micro1.D14/MISO, RE2.EncoderPinB
  N13: Pro_Micro1.D15/SCLK, RE2.EncoderPinA
  N14: Pro_Micro1.D18/A0, RE1.EncoderPinB
  N15: Pro_Micro1.D19/A1, RE1.EncoderPinA
  N16: Pro_Micro1.D20/A2, RE8.EncoderPinB
  N17: Pro_Micro1.D21/A3, RE8.EncoderPinA

custom parts:
  Pro Micro: The SparkFun Pro Micro is a complete USB-based microcontoller development system, in a very small footprint, capable of implementing many types of projects. All programming can be done via the USB port.
